# Fritzing sketch CosaWirelessReceiver (saved by Fritzing 0.8.3b)
breadboards: 1

parts:
  U2 = RWS-371 [package=THT]
  Composants1 = Arduino Uno (Rev3)
  C1 = Electrolytic Capacitor [capacitance=10µF package="100 mil [THT, electrolytic]"]

nets (from the schematic view):
  N1: U2.pin1, U2.pin_6, U2.pin_7, Composants1.GND, C1.-
  N2: U2.pin2, Composants1.D7
  N3: U2.pin_4, U2.pin_5, Composants1.5V, C1.+

custom parts:
  RWS-371: RF Receiver
